# Fritzing sketch 7ledSegments (saved by Fritzing 0.8.5b)
breadboards: 2

parts:
  U1 = atmega328 [package=dip]
  U4 = 7-SEGMENT-DISPLAY [package=7-segment-display]
  R1 = Resistor [tolerance=±5% resistance=430 package=THT]
  R3 = Resistor [tolerance=±5% resistance=430 package=THT]
  R4 = Resistor [tolerance=±5% resistance=430 package=THT]
  R5 = Resistor [tolerance=±5% resistance=430 package=THT]
  R6 = Resistor [tolerance=±5% resistance=430 package=THT]
  R7 = Resistor [tolerance=±5% resistance=430 package=THT]
  R8 = Resistor [tolerance=±5% resistance=430 package=THT]
  R9 = Resistor [tolerance=±5% resistance=430 package=THT]
  S1 = Pushbutton [package="[THT]"]
  R10 = Resistor [tolerance=±5% resistance=10k package=THT]

nets:
  N1: U1.D0_(RX), R1.Pin_0
  N2: U1.D1_(TX), R3.Pin_0
  N3: U1.D2, R9.Pin_0
  N4: U1.D3_(PWM), R6.Pin_0
  N5: U1.D4, U4.A, R7.Pin_0
  N6: U1.VCC, S1.Pin_3, S1.Pin_4
  N7: U1.GND#7, U4.C, U4.F, R10.Pin_1
  N8: U1.D5_(PWM), U4.G2, R8.Pin_0
  N9: U1.D6_(PWM), R4.Pin_0
  N10: U1.D7, R5.Pin_0
  N11: U1.A0, S1.Pin_1, S1.Pin_2, R10.Pin_0
  N12: U4.E, R6.Pin_1
  N13: U4.D, R1.Pin_1
  N14: U4.G1, R3.Pin_1
  N15: U4.DP, R4.Pin_1
  N16: U4.B, R5.Pin_1
  N17: U4.G, R9.Pin_1
